// Logisim project g1pipline.circ as structural Verilog: 19 circuits, main circuit main
module main (
);

  wire addi, alusrc, br, Branch, button_1_out, Clock, datapath_1_add, datapath_1_beq, datapath_1_sub,
       des_ex_1_alu_2, des_ex_1_jumpo_2, des_ex_1_memread_2, des_ex_1_memreg_2, des_ex_1_memwrite_2,
       des_ex_1_regdest_2, des_ex_1_regwrite_2, display_1_a, display_1_b, display_1_c, display_1_d,
       display_1_e, display_1_f, display_1_g, display_1_h, display_2_a, display_2_b, display_2_c,
       display_2_d, display_2_e, display_2_f, display_2_g, display_2_h, display_3_a, display_3_b,
       display_3_c, display_3_d, display_3_e, display_3_f, display_3_g, display_3_h, display_4_a,
       display_4_b, display_4_c, display_4_d, display_4_e, display_4_f, display_4_g, display_4_h,
       ex_1_branch_2, ex_1_jumpo_2, ex_1_memtoreg_2, ex_1_memw_2, ex_1_menread, ex_1_zero_2, EXRegWrite,
       forward_1_hazard, Jump, load, mem_1_memtoreg_2, MEMRegWrite, MemtoReg, MenRead, MenWrite, not_1_out,
       not_2_out, Regdst, RegW, Reset, salida, Stall, store, undriven, undriven_2, undriven_3, undriven_4,
       ZeroDES;
  wire [1:0] aluop, ForwardA, ForwardB;
  wire [3:0] AC, ALUcontrol_out_3, alud, displaypc_1_display1, displaypc_1_display2, displaypc_1_display3,
       displaypc_1_display4, displaypc_2_display1, displaypc_2_display2, displaypc_2_display3,
       displaypc_2_display4, displaypc_3_display1, displaypc_3_display2, displaypc_3_display3,
       displaypc_3_display4, displaypc_4_display1, displaypc_4_display2, displaypc_4_display3,
       displaypc_4_display4;
  wire [4:0] ex_1_rd_2, ex_1_rs_2, ex_1_rt_2, EXMEMrd, ID_EX_rs, ID_EX_Rt, mem_1_rd_2, mem_1_rs_2, mem_1_rt_,
       rd, rdDES, rs, rt, RW, RWFINAL;
  wire [5:0] funct, functDES, functEX, functMEM, opcode, opcodedes, opcodeex, opcodemem;
  wire [15:0] Offset;
  wire [23:0] adder_1_out, bit_extender_2_out, branch_2_br, des_ex_1_pc_1_2, ex_1_pc_3, pc_1, pcdes, pcex,
       pcif, pcinicial, pcmem;
  wire [25:0] dedodificador_1_jump, des_ex_1_jump_2, ex_1_jump_2;
  wire [31:0] ALUrs, B, Dato, ex_1_r2_2, EXra, instDES, instEX, instIF, instMEM, inti, mem_1_d_2, mem_1_ra_2,
       memoria_1_r_rs, memoria_1_r_rt, OffDES, Offsetext, R_rs_Des, R_rt_Des, RA, ram_2_data, rtmulti;

  not not_1 (not_1_out, Stall);
  Hex_Digit_Display hex_digit_display_1 (.value(displaypc_1_display1));  // open: dp
  displaypc displaypc_1 (
    .pc(pcinicial), .display1(displaypc_1_display1), .display2(displaypc_1_display2),
    .display3(displaypc_1_display3), .display4(displaypc_1_display4));
  PC u_pc_1 (
    .DirJump(ex_1_jump_2), .Clk(Clock), .pc_1(adder_1_out), .Reset(Reset), .Jump(ex_1_jumpo_2),
    .Branch(ex_1_branch_2), .Pcbranch(ex_1_pc_3), .Zero(ex_1_zero_2), .Pc(pcinicial), .Stall(not_1_out));
  Hex_Digit_Display hex_digit_display_2 (.value(displaypc_1_display2));  // open: dp
  Adder #(.width(24)) adder_1 (.a(24'h1), .b(pcinicial), .out(adder_1_out));  // open: cin, cout
  Hex_Digit_Display hex_digit_display_3 (.value(displaypc_1_display4));  // open: dp
  Hex_Digit_Display hex_digit_display_4 (.value(displaypc_1_display3));  // open: dp
  RAM #(.addrWidth(24), .dataWidth(32)) ram_1 (
    .addr(pcinicial), .data(inti), .sel(1'b1), .clk(Clock), .clr(button_1_out));  // open: ld
  Button button_1 (.out(button_1_out));
  // Probe on pcinicial
  IF if_1 (
    .Clock(Clock), .Reset(Reset), .Pc_1(adder_1_out), .Inst(inti), .Pc(pcinicial), .Pc_1_2(pc_1),
    .inst_2(instIF), .Pc_2(pcif), .Stall(Stall));
  // Probe on inti
  Clock clock_1 (.out(Clock));
  Button button_2 (.out(Reset));
  Dedodificador dedodificador_1 (
    .Entrada_Instruccion(instIF), .op(opcode), .rs(rs), .rt(rt), .rd(rd), .funct(funct),
    .Jump(dedodificador_1_jump), .Immediate_offset(Offset));  // open: shampt
  UnidadControl UC (
    .ADDI(addi), .OP(opcode), .RegDst(Regdst), .AluSrc(alusrc), .MentoReg(MemtoReg), .RegWrite(RegW),
    .MenRead(MenRead), .MenWrite(MenWrite), .Branch(Branch), .ALUOp(aluop));  // open: TipoR
  datapath datapath_1 (
    .in_1(funct), .in_2(opcode), .Add(datapath_1_add), .Sub(datapath_1_sub), .Addi(addi), .JUMP(Jump),
    .LOAD_HW(load), .STORE(store), .BEQ(datapath_1_beq));
  LED u_load (.in(load));
  Display display_1 (
    .inst(inti), .funct(funct), .a(display_1_a), .b(display_1_b), .c(display_1_c), .d(display_1_d),
    .e(display_1_e), .f(display_1_f), .g(display_1_g), .h(display_1_h));
  Hex_Digit_Display hex_digit_display_5 (.value(displaypc_2_display1));  // open: dp
  displaypc displaypc_2 (
    .pc(pcif), .display1(displaypc_2_display1), .display2(displaypc_2_display2),
    .display3(displaypc_2_display3), .display4(displaypc_2_display4));
  // Probe on rd
  LED add (.in(datapath_1_add));
  LED sub (.in(datapath_1_sub));
  LED u_addi (.in(addi));
  LED u_jump (.in(Jump));
  LED u_store (.in(store));
  LED u_branch (.in(datapath_1_beq));
  _7_Segment_Display u_7_segment_display_1 (
    .g(display_1_g), .f(display_1_f), .a(display_1_a), .b(display_1_b), .e(display_1_e), .d(display_1_d),
    .c(display_1_c), .dp(display_1_h));
  Hex_Digit_Display hex_digit_display_6 (.value(displaypc_2_display2));  // open: dp
  // Probe on pcif
  Hex_Digit_Display hex_digit_display_7 (.value(displaypc_2_display3));  // open: dp
  Hex_Digit_Display hex_digit_display_8 (.value(displaypc_2_display4));  // open: dp
  // Probe on rt
  memoria memoria_1 (
    .CLOCK(Clock), .R_rs(memoria_1_r_rs), .rs(rs), .R_rt(memoria_1_r_rt), .rt(rt), .Rw(RWFINAL), .dato(Dato),
    .Reset(Reset));
  ALUcontrol ALUcontrol (.ALUOp(aluop), .funct(funct), .out_3(ALUcontrol_out_3));
  assign Offsetext = {{16{1'b0}}, Offset};  // Bit_Extender bit_extender_1
  or or_1 (salida, addi, load, store);
  // Probe on undriven
  DES_EX des_ex_1 (
    .Clock(Clock), .Reset(Reset), .rd_2(rdDES), .MemRead_2(des_ex_1_memread_2), .pc_1_2(des_ex_1_pc_1_2),
    .Jump_2(des_ex_1_jump_2), .MemWrite_2(des_ex_1_memwrite_2), .R1_2(R_rs_Des), .rt_2(ID_EX_Rt),
    .jumpo_2(des_ex_1_jumpo_2), .Branch_2(br), .R2_2(R_rt_Des), .pc_2(pcdes), .Offset_2(OffDES),
    .ALU_2(des_ex_1_alu_2), .MemREG_2(des_ex_1_memreg_2), .RegWrite_2(des_ex_1_regwrite_2), .Pc_1(pc_1),
    .R1(memoria_1_r_rs), .R2(memoria_1_r_rt), .Offset(Offsetext), .Jump(dedodificador_1_jump), .Jumpo(Jump),
    .rd(rd), .rt(rt), .pc(pcif), .ALU(alusrc), .MemREG(MemtoReg), .RegWrite(RegW), .MemRead(MenRead),
    .MemWrite(MenWrite), .Branch(Branch), .regdest(Regdst), .regdest_2(des_ex_1_regdest_2), .Alus(alud),
    .Alud(ALUcontrol_out_3), .rs_in(rs), .rs_out(ID_EX_rs), .opcode(opcode), .opcode_2(opcodedes),
    .stall(Stall), .instruccion(instIF), .inst(instDES), .funct(funct), .funct_2(functDES));
  Hex_Digit_Display hex_digit_display_9 (.value(displaypc_3_display1));  // open: dp
  Hex_Digit_Display hex_digit_display_10 (.value(displaypc_3_display2));  // open: dp
  displaypc displaypc_3 (
    .pc(pcdes), .display1(displaypc_3_display1), .display2(displaypc_3_display2),
    .display3(displaypc_3_display3), .display4(displaypc_3_display4));
  Branch branch_2 (.PC_1(des_ex_1_pc_1_2), .Offset(OffDES), .BR(branch_2_br));
  // Probe on nothing
  Display display_2 (
    .inst(instIF), .funct(functDES), .a(display_2_a), .b(display_2_b), .c(display_2_c), .d(display_2_d),
    .e(display_2_e), .f(display_2_f), .g(display_2_g), .h(display_2_h));
  Hex_Digit_Display hex_digit_display_11 (.value(displaypc_3_display4));  // open: dp
  ALU ALU (.A(ALUrs), .B(B), .AluControl(AC), .out_4(RA), .Zero(ZeroDES));
  Multiplexer #(.width(5)) multiplexer_1 (.in0(ID_EX_Rt), .in1(rdDES), .out(RW), .sel(des_ex_1_regdest_2));  // open: en
  // Probe on RW
  Multiplexer #(.width(32)) multiplexer_2 (.in0(rtmulti), .in1(OffDES), .out(B), .sel(des_ex_1_alu_2));  // open: en
  _7_Segment_Display u_7_segment_display_2 (
    .g(display_2_g), .f(display_2_f), .a(display_2_a), .b(display_2_b), .e(display_2_e), .d(display_2_d),
    .c(display_2_c), .dp(display_2_h));
  Hex_Digit_Display hex_digit_display_12 (.value(displaypc_3_display3));  // open: dp
  Multiplexer #(.select(2), .width(32)) multiplexer_3 (
    .in0(R_rs_Des), .in1(Dato), .in2(EXra), .out(ALUrs), .sel(ForwardB));  // open: in3, en
  EX ex_1 (
    .pc(branch_2_br), .zero(ZeroDES), .ra(RA), .r2(R_rt_Des), .rw(RW), .pc_2(pcdes), .jump(des_ex_1_jump_2),
    .jumpo(des_ex_1_jumpo_2), .memtoreg(des_ex_1_memreg_2), .regw(des_ex_1_regwrite_2),
    .memread(des_ex_1_memread_2), .MemW(des_ex_1_memwrite_2), .Branch(br), .pc_3(ex_1_pc_3),
    .zero_2(ex_1_zero_2), .ra_2(EXra), .r2_2(ex_1_r2_2), .rw_2(EXMEMrd), .pc_4(pcex), .jump_2(ex_1_jump_2),
    .jumpo_2(ex_1_jumpo_2), .memtoreg_2(ex_1_memtoreg_2), .regw_2(EXRegWrite), .menread(ex_1_menread),
    .MemW_2(ex_1_memw_2), .Branch_2(ex_1_branch_2), .in_1(Clock), .Reset(Reset), .rs(ID_EX_rs),
    .rs_2(ex_1_rs_2), .rd(rdDES), .rd_2(ex_1_rd_2), .rt(ID_EX_Rt), .rt_2(ex_1_rt_2), .opcode(opcodedes),
    .opcode_2(opcodeex), .instruccion(instDES), .inst(instEX), .funct(functDES), .funct_2(functEX));
  AluBraSa alubrasa_1 (.alud(alud), .Alusalida(AC), .salida(salida), .br(br));
  // hazard hazard_1: pin names not known; wires that end beside it: rt, rd, RW, instMEM, rs, pcif, Clock, RWFINAL, pcdes, Stall
  Hex_Digit_Display hex_digit_display_13 (.value(displaypc_4_display1));  // open: dp
  displaypc displaypc_4 (
    .pc(pcex), .display1(displaypc_4_display1), .display2(displaypc_4_display2),
    .display3(displaypc_4_display3), .display4(displaypc_4_display4));
  Display display_3 (
    .inst(instDES), .funct(functEX), .a(display_3_a), .b(display_3_b), .c(display_3_c), .d(display_3_d),
    .e(display_3_e), .f(display_3_f), .g(display_3_g), .h(display_3_h));
  Multiplexer #(.select(2), .width(32)) multiplexer_4 (
    .in0(R_rt_Des), .in1(Dato), .in2(EXra), .out(rtmulti), .sel(ForwardA), .en(undriven_3));  // open: in3
  Hex_Digit_Display hex_digit_display_14 (.value(displaypc_4_display2));  // open: dp
  Hex_Digit_Display hex_digit_display_15 (.value(displaypc_4_display4));  // open: dp
  Bit_Extender #(.in_width(32), .out_width(24)) bit_extender_2 (.in(EXra), .out(bit_extender_2_out));
  // Probe on undriven_2
  _7_Segment_Display u_7_segment_display_3 (
    .g(display_3_g), .f(display_3_f), .a(display_3_a), .b(display_3_b), .e(display_3_e), .d(display_3_d),
    .c(display_3_c), .dp(display_3_h));
  Hex_Digit_Display hex_digit_display_16 (.value(displaypc_4_display3));  // open: dp
  // Probe on rt
  RAM #(.addrWidth(24), .dataWidth(32), .bus("separate")) ram_2 (
    .addr(bit_extender_2_out), .din(ex_1_r2_2), .data(ram_2_data), .clk(Clock), .ld(not_2_out), .clr(Reset));  // open: str, sel
  not not_2 (not_2_out, ex_1_memw_2);
  // Probe on pcex
  LED led_1 (.in(forward_1_hazard));
  forward forward_1 (
    .EX_MEM_RegWrite(EXRegWrite), .hazard(forward_1_hazard), .EX_MEM_Rd(EXMEMrd), .ID_EX_Rt(ID_EX_Rt),
    .ID_EX_Rs(ID_EX_rs), .ForwardA(ForwardA), .ForwardB(ForwardB), .MEM_WB_RegWr(MEMRegWrite),
    .MEM_WB_Rd(RWFINAL));
  // Probe on undriven_4
  Multiplexer #(.width(32)) multiplexer_5 (
    .in0(mem_1_ra_2), .in1(mem_1_d_2), .out(Dato), .sel(mem_1_memtoreg_2));  // open: en
  MEM mem_1 (
    .RA(EXra), .D(ram_2_data), .rw(EXMEMrd), .pc(pcex), .rs(ex_1_rs_2), .rd(ex_1_rd_2), .rt(ex_1_rt_2),
    .MemToReg(ex_1_memtoreg_2), .Regw(EXRegWrite), .MemRead(ex_1_menread), .RA_2(mem_1_ra_2),
    .D_2(mem_1_d_2), .rw_2(RWFINAL), .pc_2(pcmem), .rs_2(mem_1_rs_2), .rd_2(mem_1_rd_2), .rt_(mem_1_rt_),
    .MemToReg_2(mem_1_memtoreg_2), .RegW_2(MEMRegWrite), .clk(Clock), .reset(Reset), .opcode(opcodeex),
    .opcode_2(opcodemem), .instruccion(instEX), .inst(instMEM), .funct(functEX), .funct_2(functMEM));  // open: MemRead_2
  // Probe on mem_1_rs_2
  // Probe on mem_1_rd_2
  // Probe on mem_1_rt_
  Display display_4 (
    .inst(instEX), .funct(functMEM), .a(display_4_a), .b(display_4_b), .c(display_4_c), .d(display_4_d),
    .e(display_4_e), .f(display_4_f), .g(display_4_g), .h(display_4_h));
  // Probe on Dato
  _7_Segment_Display u_7_segment_display_4 (
    .g(display_4_g), .f(display_4_f), .a(display_4_a), .b(display_4_b), .e(display_4_e), .d(display_4_d),
    .c(display_4_c), .dp(display_4_h));
  // Probe on instMEM

  // Other names for the same wires on the sheet: rtDES[4:0] = ID_EX_Rt

  // Notes on the sheet:
  //   Pc en decimal
  //   Autores:
  //   Juan Bojato
  //   Pc if
  //   Juan Buelvas
  //   Pc en hexadecimal
  //   Jaime Ramos
  //   IF/DEC
  //   Pc en decimal
  //   Pc des
  //   Tipos de instrucciones
  //   _ = R
  //   A.=Addi
  //   J = Jump
  //   Instrucciones IF
  //   Pc en hexadecimal
  //   L = Load
  //   S = Store
  //   B = Branch
  //   DES/EX
  //   Pc en decimal
  //   Instrucciones DES/EX
  //   Pc EX
  //   Pc en hexadecimal
  //   EX
  //   Pc en decimal
  //   Instrucciones EX
  //   Pc MEM
  //   Pc en hexadecimal
  //   MEM
  //   Instrucciones MEM
endmodule

module rama (
  input  [15:0] in_1
);

  wire and_1_out, branch, Zero;
  wire [23:0] adder_1_out, bit_extender_1_out, multiplexer_1_out, pc_1, subtractor_1_out;

  assign bit_extender_1_out = {{9{1'b0}}, in_1[14:0]};  // Bit_Extender bit_extender_1
  Adder #(.width(24)) adder_1 (.a(pc_1), .b(bit_extender_1_out), .out(adder_1_out));  // open: cin, cout
  Subtractor #(.width(24)) subtractor_1 (.a(pc_1), .b(bit_extender_1_out), .out(subtractor_1_out));  // open: bin, bout
  Multiplexer #(.width(24), .enable("false")) multiplexer_1 (
    .in0(adder_1_out), .in1(subtractor_1_out), .out(multiplexer_1_out), .sel(in_1[15]));
  Multiplexer #(.width(24), .enable("false")) multiplexer_2 (
    .in0(pc_1), .in1(multiplexer_1_out), .sel(and_1_out));  // open: out
  and and_1 (and_1_out, Zero, branch);

  // Other names for the same wires on the sheet: imm[15:0] = in_1

  // Notes on the sheet:
  //   Branch
endmodule

module PC (
  input  [25:0] DirJump,
  input  Stall,
  input  Clk,
  input  [23:0] pc_1,
  input  Reset,
  input  Jump,
  input  Branch,
  input  [23:0] Pcbranch,
  input  Zero,
  output [23:0] Pc
);

  wire and_1_out;
  wire [23:0] multiplexer_1_out, multiplexer_2_out;

  Register #(.width(24)) u_Pc (.D(multiplexer_2_out), .en(Stall), .Q(Pc), .clk(Clk), .clr(Reset));
  Multiplexer #(.width(24), .enable("false")) multiplexer_1 (
    .in0(pc_1), .in1(Pcbranch), .out(multiplexer_1_out), .sel(and_1_out));
  and and_1 (and_1_out, Branch, Zero);
  Multiplexer #(.width(24), .enable("false")) multiplexer_2 (
    .in0(multiplexer_1_out), .in1(DirJump[23:0]), .out(multiplexer_2_out), .sel(Jump));
endmodule

// Decodificador
module Dedodificador (
  input  [31:0] Entrada_Instruccion,
  output [5:0] op,
  output [4:0] rs,
  output [4:0] rt,
  output [4:0] rd,
  output [4:0] shampt,
  output [5:0] funct,
  output [25:0] Jump,
  output [15:0] Immediate_offset
);


  assign funct = Entrada_Instruccion[5:0];
  assign Immediate_offset = Entrada_Instruccion[15:0];
  assign Jump = Entrada_Instruccion[25:0];
  assign op = Entrada_Instruccion[31:26];
  assign rd = Entrada_Instruccion[15:11];
  assign rs = Entrada_Instruccion[25:21];
  assign rt = Entrada_Instruccion[20:16];
  assign shampt = Entrada_Instruccion[10:6];

  // Notes on the sheet:
  //   Instruccion tipo R
endmodule

module datapath (
  input  [5:0] in_1,
  input  [5:0] in_2,
  output Add,
  output Sub,
  output Addi,
  output JUMP,
  output LOAD_HW,
  output STORE,
  output BEQ
);

  wire comparator_1_eq, comparator_2_eq, comparator_3_eq, comparator_9_eq;

  Comparator #(.width(6)) comparator_1 (.a(in_1), .b(6'b100000), .eq(comparator_1_eq));  // open: gt, lt
  Comparator #(.width(6)) comparator_2 (.a(in_2), .b({6{1'b0}}), .eq(comparator_2_eq));  // open: gt, lt
  Comparator #(.width(6)) comparator_3 (.a(in_1), .b(6'b100010), .eq(comparator_3_eq));  // open: gt, lt
  Comparator #(.width(6)) comparator_4 (.a(in_2), .b(6'b001000), .eq(Addi));  // open: gt, lt
  Comparator #(.width(6)) comparator_5 (.a(in_2), .b(6'b000010), .eq(JUMP));  // open: gt, lt
  Comparator #(.width(6)) comparator_6 (.a(in_2), .b(6'b100011), .eq(LOAD_HW));  // open: gt, lt
  Comparator #(.width(6)) comparator_7 (.a(in_2), .b(6'b101011), .eq(STORE));  // open: gt, lt
  Comparator #(.width(6)) comparator_8 (.a(in_2), .b(6'b000100), .eq(BEQ));  // open: gt, lt
  Comparator #(.width(6)) comparator_9 (.a(in_2), .b({6{1'b0}}), .eq(comparator_9_eq));  // open: gt, lt
  and and_1 (Add, comparator_1_eq, comparator_2_eq);
  and and_2 (Sub, comparator_3_eq, comparator_9_eq);
endmodule

// Registros
module memoria (
  input  CLOCK,
  input  [4:0] rs,
  input  [4:0] rt,
  input  Reset,
  input  [4:0] Rw,
  input  [31:0] dato,
  output [31:0] R_rs,
  output [31:0] R_rt
);

  wire _0A, _0B, _0C, _0D, _1A, _1B, _1C, _1D, _2A, _2B, _2C, _2D, _3A, _3B, _3C, _3D, _4A, _4B, _4C, _4D,
       _5A, _5B, _5C, _5D, _6A, _6B, _6C, _6D, _7A, _7B, _7C, _7D;
  wire [31:0] _0, _1, _2, _3, _4, _5, _6, _7, _8, _9, _10, _11, _12, _13, _14, _15, _16, _17, _18, _19, _20,
       _21, _22, _23, _24, _25, _26, _27, _28, _29, _30, _31;

  Multiplexer #(.select(5), .width(32)) multiplexer_1 (
    .in0(_0), .in1(_1), .in2(_2), .in3(_3), .in4(_4), .in5(_5), .in6(_6), .in7(_7), .in8(_8), .in9(_9),
    .in10(_10), .in11(_11), .in12(_12), .in13(_13), .in14(_14), .in15(_15), .in16(_16), .in17(_17),
    .in18(_18), .in19(_19), .in20(_20), .in21(_21), .in22(_22), .in23(_23), .in24(_24), .in25(_25),
    .in26(_26), .in27(_27), .in28(_28), .in29(_29), .in30(_30), .in31(_31), .out(R_rs), .sel(rs));  // open: en
  Multiplexer #(.select(5), .width(32)) multiplexer_2 (
    .in0(_0), .in1(_1), .in2(_2), .in3(_3), .in4(_4), .in5(_5), .in6(_6), .in7(_7), .in8(_8), .in9(_9),
    .in10(_10), .in11(_11), .in12(_12), .in13(_13), .in14(_14), .in15(_15), .in16(_16), .in17(_17),
    .in18(_18), .in19(_19), .in20(_20), .in21(_21), .in22(_22), .in23(_23), .in24(_24), .in25(_25),
    .in26(_26), .in27(_27), .in28(_28), .in29(_29), .in30(_30), .in31(_31), .out(R_rt), .sel(rt));  // open: en
  Demultiplexer #(.select(5)) demultiplexer_1 (
    .out0(_0A), .out1(_1A), .out2(_2A), .out3(_3A), .out4(_4A), .out5(_5A), .out6(_6A), .out7(_7A),
    .out8(_0B), .out9(_1B), .out10(_2B), .out11(_3B), .out12(_4B), .out13(_5B), .out14(_6B), .out15(_7B),
    .out16(_0C), .out17(_1C), .out18(_2C), .out19(_3C), .out20(_4C), .out21(_5C), .out22(_6C), .out23(_7C),
    .out24(_0D), .out25(_1D), .out26(_2D), .out27(_3D), .out28(_4D), .out29(_5D), .out30(_6D), .out31(_7D),
    .in(1'b1), .sel(Rw));  // open: en
  Register #(.width(32)) u__0 (.D(dato), .en(_0A), .Q(_0), .clk(CLOCK), .clr(Reset));
  Register #(.width(32)) u__8 (.D(dato), .en(_0B), .Q(_8), .clk(CLOCK), .clr(Reset));
  Register #(.width(32)) u__16 (.D(dato), .en(_0C), .Q(_16), .clk(CLOCK), .clr(Reset));
  Register #(.width(32)) u__24 (.D(dato), .en(_0D), .Q(_24), .clk(CLOCK), .clr(Reset));
  Register #(.width(32)) u__1 (.D(dato), .en(_1A), .Q(_1), .clk(CLOCK), .clr(Reset));
  Register #(.width(32)) u__9 (.D(dato), .en(_1B), .Q(_9), .clk(CLOCK), .clr(Reset));
  Register #(.width(32)) u__17 (.D(dato), .en(_1C), .Q(_17), .clk(CLOCK), .clr(Reset));
  Register #(.width(32)) u__25 (.D(dato), .en(_1D), .Q(_25), .clk(CLOCK), .clr(Reset));
  Register #(.width(32)) u__2 (.D(dato), .en(_2A), .Q(_2), .clk(CLOCK), .clr(Reset));
  Register #(.width(32)) u__10 (.D(dato), .en(_2B), .Q(_10), .clk(CLOCK), .clr(Reset));
  Register #(.width(32)) u__18 (.D(dato), .en(_2C), .Q(_18), .clk(CLOCK), .clr(Reset));
  Register #(.width(32)) u__26 (.D(dato), .en(_2D), .Q(_26), .clk(CLOCK), .clr(Reset));
  Register #(.width(32)) u__3 (.D(dato), .en(_3A), .Q(_3), .clk(CLOCK), .clr(Reset));
  Register #(.width(32)) u__11 (.D(dato), .en(_3B), .Q(_11), .clk(CLOCK), .clr(Reset));
  Register #(.width(32)) u__19 (.D(dato), .en(_3C), .Q(_19), .clk(CLOCK), .clr(Reset));
  Register #(.width(32)) u__27 (.D(dato), .en(_3D), .Q(_27), .clk(CLOCK), .clr(Reset));
  Register #(.width(32)) u__4 (.D(dato), .en(_4A), .Q(_4), .clk(CLOCK), .clr(Reset));
  Register #(.width(32)) u__12 (.D(dato), .en(_4B), .Q(_12), .clk(CLOCK), .clr(Reset));
  Register #(.width(32)) u__20 (.D(dato), .en(_4C), .Q(_20), .clk(CLOCK), .clr(Reset));
  Register #(.width(32)) u__28 (.D(dato), .en(_4D), .Q(_28), .clk(CLOCK), .clr(Reset));
  Register #(.width(32)) u__5 (.D(dato), .en(_5A), .Q(_5), .clk(CLOCK), .clr(Reset));
  Register #(.width(32)) u__13 (.D(dato), .en(_5B), .Q(_13), .clk(CLOCK), .clr(Reset));
  Register #(.width(32)) u__21 (.D(dato), .en(_5C), .Q(_21), .clk(CLOCK), .clr(Reset));
  Register #(.width(32)) u__29 (.D(dato), .en(_5D), .Q(_29), .clk(CLOCK), .clr(Reset));
  Register #(.width(32)) u__6 (.D(dato), .en(_6A), .Q(_6), .clk(CLOCK), .clr(Reset));
  Register #(.width(32)) u__14 (.D(dato), .en(_6B), .Q(_14), .clk(CLOCK), .clr(Reset));
  Register #(.width(32)) u__22 (.D(dato), .en(_6C), .Q(_22), .clk(CLOCK), .clr(Reset));
  Register #(.width(32)) u__30 (.D(dato), .en(_6D), .Q(_30), .clk(CLOCK), .clr(Reset));
  Register #(.width(32)) u__7 (.D(dato), .en(_7A), .Q(_7), .clk(CLOCK), .clr(Reset));
  Register #(.width(32)) u__15 (.D(dato), .en(_7B), .Q(_15), .clk(CLOCK), .clr(Reset));
  Register #(.width(32)) u__23 (.D(dato), .en(_7C), .Q(_23), .clk(CLOCK), .clr(Reset));
  Register #(.width(32)) u__31 (.D(dato), .en(_7D), .Q(_31), .clk(CLOCK), .clr(Reset));
endmodule

module UnidadControl (
  input  ADDI,
  input  [5:0] OP,
  output RegDst,
  output AluSrc,
  output MentoReg,
  output RegWrite,
  output MenRead,
  output MenWrite,
  output Branch,
  output TipoR,
  output [1:0] ALUOp
);

  wire and_1_out, and_2_out, and_3_out, and_4_out, not_1_out, not_2_out, not_3_out, not_4_out, not_5_out,
       not_6_out, not_7_out, not_8_out, not_9_out, not_10_out, not_11_out, not_12_out, not_13_out,
       not_14_out, not_15_out, not_16_out, not_17_out, not_18_out, not_19_out, not_20_out, not_21_out,
       not_22_out, not_23_out, not_24_out, not_25_out, not_26_out, not_27_out;

  Comparator #(.width(6)) comparator_1 (.a(OP), .b({6{1'b0}}), .eq(TipoR));  // open: gt, lt
  not not_1 (not_1_out, OP[1]);
  not not_2 (not_2_out, OP[2]);
  not not_3 (not_3_out, OP[4]);
  not not_4 (not_4_out, OP[5]);
  not not_5 (not_5_out, OP[5]);
  not not_6 (not_6_out, OP[4]);
  not not_7 (not_7_out, OP[2]);
  not not_8 (not_8_out, OP[1]);
  not not_9 (not_9_out, OP[0]);
  not not_10 (not_10_out, OP[3]);
  not not_11 (not_11_out, OP[1]);
  not not_12 (not_12_out, ADDI);
  and and_1 (and_1_out, not_1_out, not_2_out, OP[3], not_3_out, not_4_out);
  and and_2 (and_2_out, not_5_out, not_6_out, not_7_out, not_8_out, not_9_out);
  not not_13 (not_13_out, OP[3]);
  and and_3 (and_3_out, not_13_out, not_14_out);
  not not_14 (not_14_out, OP[2]);
  and and_4 (and_4_out, not_10_out, OP[1]);
  and and_5 (RegDst, not_11_out, not_12_out);
  or or_1 (AluSrc, OP[1], and_1_out);
  or or_2 (RegWrite, and_2_out, and_3_out);
  not not_15 (not_15_out, ADDI);
  and and_6 (MenWrite, OP[3], not_16_out);
  not not_16 (not_16_out, ADDI);
  not not_17 (not_17_out, OP[5]);
  not not_18 (not_18_out, OP[4]);
  not not_19 (not_19_out, OP[3]);
  not not_20 (not_20_out, OP[2]);
  not not_21 (not_21_out, OP[1]);
  not not_22 (not_22_out, OP[0]);
  not not_23 (not_23_out, OP[5]);
  not not_24 (not_24_out, OP[4]);
  not not_25 (not_25_out, OP[3]);
  not not_26 (not_26_out, OP[1]);
  not not_27 (not_27_out, OP[0]);
  and and_7 (MenRead, and_4_out, not_15_out);
  and and_8 (ALUOp[1], not_17_out, not_18_out, not_19_out, not_20_out, not_21_out, not_22_out);
  and and_9 (ALUOp[0], not_23_out, not_24_out, not_25_out, OP[2], not_26_out, not_27_out);

  assign Branch = OP[2];
  assign MentoReg = OP[1];
endmodule

module ALU (
  input  [31:0] A,
  input  [31:0] B,
  input  [3:0] AluControl,
  output [31:0] out_4,
  output Zero
);

  wire comparator_1_eq, comparator_2_eq, comparator_3_eq, comparator_4_eq;
  wire [2:0] priority_encoder_1_out;
  wire [31:0] add, \and , \or , Sub;

  Comparator #(.width(4)) comparator_1 (.a(AluControl), .b(4'b0010), .eq(comparator_1_eq));  // open: gt, lt
  Comparator #(.width(4)) comparator_2 (.a(AluControl), .b(4'b0110), .eq(comparator_2_eq));  // open: gt, lt
  Comparator #(.width(4)) comparator_3 (.a(AluControl), .b(4'b0000), .eq(comparator_3_eq));  // open: gt, lt
  Comparator #(.width(4)) comparator_4 (.a(AluControl), .b(4'b0001), .eq(comparator_4_eq));  // open: gt, lt
  Adder #(.width(32)) adder_1 (.a(A), .b(B), .out(add));  // open: cin, cout
  Subtractor #(.width(32)) subtractor_1 (.a(A), .b(B), .out(Sub));  // open: bin, bout
  Comparator #(.width(32)) comparator_5 (.a(A), .b(B), .eq(Zero));  // open: gt, lt
  Priority_Encoder priority_encoder_1 (
    .in0(comparator_1_eq), .in1(comparator_2_eq), .in2(comparator_3_eq), .in3(comparator_4_eq),
    .out(priority_encoder_1_out));  // open: in4, in5, in6, in7, en_in, gs, en_out
  assign \and  = A & B;  // AND_Gate and_1, 32 bits wide
  assign \or  = A | B;  // OR_Gate or_1, 32 bits wide
  Multiplexer #(.select(3), .width(32), .enable("false")) multiplexer_1 (
    .in0(add), .in1(Sub), .in2(\and ), .in3(\or ), .out(out_4), .sel(priority_encoder_1_out));  // open: in4, in5, in6, in7

  // Notes on the sheet:
  //   Add
  //   0010
  //   Substract
  //   0110
  //   and
  //   0000
  //   or
  //   0001
endmodule

module ALUcontrol (
  input  [1:0] ALUOp,
  input  [5:0] funct,
  output [3:0] out_3
);

  wire and_1_out, and_2_out, and_3_out, and_4_out, and_5_out, and_6_out, not_1_out, not_2_out, not_3_out,
       not_4_out, not_5_out, not_6_out, not_7_out, not_8_out;

  not not_1 (not_1_out, ALUOp[1]);
  not not_2 (not_2_out, funct[2]);
  not not_3 (not_3_out, ALUOp[1]);
  not not_4 (not_4_out, funct[2]);
  not not_5 (not_5_out, funct[3]);
  not not_6 (not_6_out, funct[1]);
  not not_7 (not_7_out, funct[2]);
  not not_8 (not_8_out, funct[0]);
  and and_1 (and_1_out, not_1_out, ALUOp[0]);
  and and_2 (and_2_out, ALUOp[1], not_2_out, funct[0]);
  and and_3 (and_3_out, ALUOp[1], funct[1]);
  and and_4 (and_4_out, ALUOp[1], funct[3]);
  or or_1 (out_3[1], not_3_out, not_4_out, funct[1], funct[3]);
  and and_5 (and_5_out, ALUOp[1], not_5_out, funct[2], not_6_out, funct[0]);
  and and_6 (and_6_out, ALUOp[1], funct[3], not_7_out, funct[1], not_8_out);
  or or_2 (out_3[2], and_1_out, and_2_out, and_3_out, and_4_out);
  or or_3 (out_3[0], and_5_out, and_6_out);

  assign out_3[3] = 1'b0;
endmodule

module IF (
  input  Clock,
  input  Reset,
  input  [23:0] Pc_1,
  input  [31:0] Inst,
  input  [23:0] Pc,
  input  Stall,
  output [23:0] Pc_1_2,
  output [31:0] inst_2,
  output [23:0] Pc_2
);

  wire not_1_out;

  not not_1 (not_1_out, Stall);
  Register #(.width(24)) register_1 (.D(Pc_1), .en(not_1_out), .Q(Pc_1_2), .clk(Clock), .clr(Reset));
  Register #(.width(32)) register_2 (.D(Inst), .en(not_1_out), .Q(inst_2), .clk(Clock), .clr(Reset));
  Register #(.width(24)) register_3 (.D(Pc), .en(not_1_out), .Q(Pc_2), .clk(Clock), .clr(Reset));
endmodule

module DES_EX (
  input  Clock,
  input  Reset,
  input  stall,
  input  [4:0] rd,
  input  MemRead,
  input  [23:0] Pc_1,
  input  [31:0] Offset,
  input  MemWrite,
  input  [31:0] R1,
  input  ALU,
  input  [4:0] rt,
  input  [25:0] Jump,
  input  Branch,
  input  MemREG,
  input  [31:0] R2,
  input  Jumpo,
  input  [23:0] pc,
  input  regdest,
  input  RegWrite,
  input  [31:0] instruccion,
  input  [5:0] opcode,
  input  [3:0] Alud,
  input  [4:0] rs_in,
  input  [5:0] funct,
  output [4:0] rd_2,
  output [23:0] pc_1_2,
  output MemRead_2,
  output [31:0] Offset_2,
  output MemWrite_2,
  output [31:0] R1_2,
  output ALU_2,
  output [4:0] rt_2,
  output [25:0] Jump_2,
  output Branch_2,
  output MemREG_2,
  output [31:0] R2_2,
  output [23:0] pc_2,
  output regdest_2,
  output jumpo_2,
  output RegWrite_2,
  output [5:0] opcode_2,
  output [3:0] Alus,
  output [4:0] rs_out,
  output [31:0] inst,
  output [5:0] funct_2
);

  wire clock_t, multiplexer_5_out, multiplexer_13_out, multiplexer_14_out, multiplexer_15_out,
       multiplexer_16_out, multiplexer_17_out, multiplexer_18_out, multiplexer_19_out;
  wire [3:0] multiplexer_20_out;
  wire [4:0] multiplexer_6_out, multiplexer_9_out, multiplexer_10_out;
  wire [5:0] multiplexer_11_out, multiplexer_21_out;
  wire [23:0] multiplexer_1_out, multiplexer_12_out;
  wire [25:0] multiplexer_8_out;
  wire [31:0] multiplexer_2_out, multiplexer_3_out, multiplexer_4_out, multiplexer_7_out;

  not not_1 (clock_t, Clock);
  Multiplexer #(.width(24)) multiplexer_1 (
    .in0(Pc_1), .in1({24{1'b0}}), .out(multiplexer_1_out), .sel(stall));  // open: en
  Multiplexer #(.width(32)) multiplexer_2 (
    .in0(R1), .in1({32{1'b0}}), .out(multiplexer_2_out), .sel(stall));  // open: en
  Multiplexer #(.width(32)) multiplexer_3 (
    .in0(R2), .in1({32{1'b0}}), .out(multiplexer_3_out), .sel(stall));  // open: en
  Register #(.width(24)) register_1 (.D(multiplexer_1_out), .Q(pc_1_2), .clk(clock_t), .clr(Reset));  // open: en
  Register #(.width(32)) register_2 (.D(multiplexer_2_out), .Q(R1_2), .clk(clock_t), .clr(Reset));  // open: en
  Register #(.width(32)) register_3 (.D(multiplexer_3_out), .Q(R2_2), .clk(clock_t), .clr(Reset));  // open: en
  Register #(.width(32)) register_4 (.D(multiplexer_4_out), .Q(inst), .clk(clock_t), .clr(Reset));  // open: en
  Multiplexer #(.width(32)) multiplexer_4 (
    .in0(instruccion), .in1({32{1'b0}}), .out(multiplexer_4_out), .sel(stall));  // open: en
  Multiplexer multiplexer_5 (.in0(Jumpo), .in1(1'b0), .out(multiplexer_5_out), .sel(stall));  // open: en
  Multiplexer #(.width(5)) multiplexer_6 (
    .in0(rs_in), .in1({5{1'b0}}), .out(multiplexer_6_out), .sel(stall));  // open: en
  Multiplexer #(.width(32)) multiplexer_7 (
    .in0(Offset), .in1({32{1'b0}}), .out(multiplexer_7_out), .sel(stall));  // open: en
  Multiplexer #(.width(26)) multiplexer_8 (
    .in0(Jump), .in1({26{1'b0}}), .out(multiplexer_8_out), .sel(stall));  // open: en
  Register #(.width(1)) register_5 (.D(multiplexer_5_out), .Q(jumpo_2), .clk(clock_t), .clr(Reset));  // open: en
  Register #(.width(5)) register_6 (.D(multiplexer_6_out), .Q(rs_out), .clk(clock_t), .clr(Reset));  // open: en
  Register #(.width(32)) register_7 (.D(multiplexer_7_out), .Q(Offset_2), .clk(clock_t), .clr(Reset));  // open: en
  Register #(.width(26)) register_8 (.D(multiplexer_8_out), .Q(Jump_2), .clk(clock_t), .clr(Reset));  // open: en
  Multiplexer #(.width(5)) multiplexer_9 (.in0(rd), .in1({5{1'b0}}), .out(multiplexer_9_out), .sel(stall));  // open: en
  Multiplexer #(.width(5)) multiplexer_10 (
    .in0(rt), .in1({5{1'b0}}), .out(multiplexer_10_out), .sel(stall));  // open: en
  Multiplexer #(.width(6)) multiplexer_11 (
    .in0(opcode), .in1({6{1'b0}}), .out(multiplexer_11_out), .sel(stall));  // open: en
  Register #(.width(5)) register_9 (.D(multiplexer_9_out), .Q(rd_2), .clk(clock_t), .clr(Reset));  // open: en
  Register #(.width(5)) register_10 (.D(multiplexer_10_out), .Q(rt_2), .clk(clock_t), .clr(Reset));  // open: en
  Register #(.width(24)) register_11 (.D(multiplexer_12_out), .Q(pc_2), .clk(clock_t), .clr(Reset));  // open: en
  Multiplexer #(.width(24)) multiplexer_12 (
    .in0(pc), .in1({24{1'b0}}), .out(multiplexer_12_out), .sel(stall));  // open: en
  Register #(.width(6)) register_12 (.D(multiplexer_11_out), .Q(opcode_2), .clk(clock_t), .clr(Reset));  // open: en
  Multiplexer multiplexer_13 (.in0(ALU), .in1(1'b0), .out(multiplexer_13_out), .sel(stall));  // open: en
  Multiplexer multiplexer_14 (.in0(MemREG), .in1(1'b0), .out(multiplexer_14_out), .sel(stall));  // open: en
  Multiplexer multiplexer_15 (.in0(RegWrite), .in1(1'b0), .out(multiplexer_15_out), .sel(stall));  // open: en
  Register #(.width(1)) register_13 (.D(multiplexer_13_out), .Q(ALU_2), .clk(clock_t), .clr(Reset));  // open: en
  Register #(.width(1)) register_14 (.D(multiplexer_14_out), .Q(MemREG_2), .clk(clock_t), .clr(Reset));  // open: en
  Register #(.width(1)) register_15 (.D(multiplexer_15_out), .Q(RegWrite_2), .clk(clock_t), .clr(Reset));  // open: en
  Multiplexer multiplexer_16 (.in0(MemRead), .in1(1'b0), .out(multiplexer_16_out), .sel(stall));  // open: en
  Multiplexer multiplexer_17 (.in0(MemWrite), .in1(1'b0), .out(multiplexer_17_out), .sel(stall));  // open: en
  Multiplexer multiplexer_18 (.in0(Branch), .in1(1'b0), .out(multiplexer_18_out), .sel(stall));  // open: en
  Multiplexer multiplexer_19 (.in0(regdest), .in1(1'b0), .out(multiplexer_19_out), .sel(stall));  // open: en
  Multiplexer #(.width(4)) multiplexer_20 (
    .in0(Alud), .in1(4'b0000), .out(multiplexer_20_out), .sel(stall));  // open: en
  Multiplexer #(.width(6)) multiplexer_21 (
    .in0(funct), .in1({6{1'b0}}), .out(multiplexer_21_out), .sel(stall));  // open: en
  Register #(.width(1)) register_16 (.D(multiplexer_19_out), .Q(regdest_2), .clk(clock_t), .clr(Reset));  // open: en
  Register #(.width(4)) register_17 (.D(multiplexer_20_out), .Q(Alus), .clk(clock_t), .clr(Reset));  // open: en
  Register #(.width(1)) register_18 (.D(multiplexer_16_out), .Q(MemRead_2), .clk(clock_t), .clr(Reset));  // open: en
  Register #(.width(1)) register_19 (.D(multiplexer_17_out), .Q(MemWrite_2), .clk(clock_t), .clr(Reset));  // open: en
  Register #(.width(1)) register_20 (.D(multiplexer_18_out), .Q(Branch_2), .clk(clock_t), .clr(Reset));  // open: en
  Register #(.width(6)) register_21 (.D(multiplexer_21_out), .Q(funct_2), .clk(clock_t), .clr(Reset));  // open: en
endmodule

module EX (
  input  in_1,
  input  Reset,
  input  [23:0] pc,
  input  zero,
  input  [31:0] ra,
  input  [31:0] r2,
  input  [4:0] rs,
  input  [4:0] rd,
  input  [4:0] rt,
  input  [4:0] rw,
  input  [23:0] pc_2,
  input  [25:0] jump,
  input  [5:0] opcode,
  input  jumpo,
  input  memtoreg,
  input  regw,
  input  memread,
  input  MemW,
  input  Branch,
  input  [31:0] instruccion,
  input  [5:0] funct,
  output [23:0] pc_3,
  output zero_2,
  output [31:0] ra_2,
  output [31:0] r2_2,
  output [4:0] rs_2,
  output [4:0] rd_2,
  output [4:0] rt_2,
  output [4:0] rw_2,
  output [23:0] pc_4,
  output [25:0] jump_2,
  output [5:0] opcode_2,
  output jumpo_2,
  output memtoreg_2,
  output regw_2,
  output menread,
  output MemW_2,
  output Branch_2,
  output [31:0] inst,
  output [5:0] funct_2
);

  wire clk;

  not not_1 (clk, in_1);
  Register #(.width(5)) register_1 (.D(rs), .Q(rs_2), .clk(clk), .clr(Reset));  // open: en
  Register #(.width(5)) register_2 (.D(rd), .Q(rd_2), .clk(clk), .clr(Reset));  // open: en
  Register #(.width(5)) register_3 (.D(rt), .Q(rt_2), .clk(clk), .clr(Reset));  // open: en
  Register #(.width(6)) register_4 (.D(opcode), .Q(opcode_2), .clk(clk), .clr(Reset));  // open: en
  Register #(.width(1)) register_5 (.D(jumpo), .Q(jumpo_2), .clk(clk), .clr(Reset));  // open: en
  Register #(.width(24)) register_6 (.D(pc), .Q(pc_3), .clk(clk), .clr(Reset));  // open: en
  Register #(.width(1)) register_7 (.D(zero), .Q(zero_2), .clk(clk), .clr(Reset));  // open: en
  Register #(.width(32)) register_8 (.D(ra), .Q(ra_2), .clk(clk), .clr(Reset));  // open: en
  Register #(.width(32)) register_9 (.D(r2), .Q(r2_2), .clk(clk), .clr(Reset));  // open: en
  Register #(.width(5)) register_10 (.D(rw), .Q(rw_2), .clk(clk), .clr(Reset));  // open: en
  Register #(.width(24)) register_11 (.D(pc_2), .Q(pc_4), .clk(clk), .clr(Reset));  // open: en
  Register #(.width(26)) register_12 (.D(jump), .Q(jump_2), .clk(clk), .clr(Reset));  // open: en
  Register #(.width(1)) register_13 (.D(memtoreg), .Q(memtoreg_2), .clk(clk), .clr(Reset));  // open: en
  Register #(.width(1)) register_14 (.D(regw), .Q(regw_2), .clk(clk), .clr(Reset));  // open: en
  Register #(.width(1)) register_15 (.D(memread), .Q(menread), .clk(clk), .clr(Reset));  // open: en
  Register #(.width(1)) register_16 (.D(MemW), .Q(MemW_2), .clk(clk), .clr(Reset));  // open: en
  Register #(.width(1)) register_17 (.D(Branch), .Q(Branch_2), .clk(clk), .clr(Reset));  // open: en
  Register #(.width(6)) register_18 (.D(funct), .Q(funct_2), .clk(clk), .clr(Reset));  // open: en
  Register #(.width(32)) register_19 (.D(instruccion), .Q(inst), .clk(clk), .clr(Reset));  // open: en

  // Other names for the same wires on the sheet: res = Reset
endmodule

module AluBraSa (
  input  [3:0] alud,
  input  salida,
  input  br,
  output [3:0] Alusalida
);

  assign Alusalida = alud | {4{br}} | {{2{alud[3]}}, salida, alud[3]};  // OR_Gate or_1, 4 bits wide
endmodule

module Branch (
  input  [23:0] PC_1,
  input  [31:0] Offset,
  output [23:0] BR
);

  wire [15:0] bit_extender_1_out;
  wire [23:0] adder_1_out, bit_extender_2_out, subtractor_1_out;

  Bit_Extender #(.in_width(32)) bit_extender_1 (.in(Offset), .out(bit_extender_1_out));
  assign bit_extender_2_out = {{9{1'b0}}, bit_extender_1_out[14:0]};  // Bit_Extender bit_extender_2
  Adder #(.width(24)) adder_1 (.a(PC_1), .b(bit_extender_2_out), .out(adder_1_out));  // open: cin, cout
  Subtractor #(.width(24)) subtractor_1 (.a(PC_1), .b(bit_extender_2_out), .out(subtractor_1_out));  // open: bin, bout
  Multiplexer #(.width(24), .enable("false")) multiplexer_1 (
    .in0(adder_1_out), .in1(subtractor_1_out), .out(BR), .sel(bit_extender_1_out[15]));
endmodule

module MEM (
  input  clk,
  input  reset,
  input  [31:0] RA,
  input  [5:0] opcode,
  input  [31:0] D,
  input  [4:0] rw,
  input  [23:0] pc,
  input  [4:0] rs,
  input  [4:0] rd,
  input  [4:0] rt,
  input  MemToReg,
  input  Regw,
  input  MemRead,
  input  [31:0] instruccion,
  input  [5:0] funct,
  output [31:0] RA_2,
  output [5:0] opcode_2,
  output [31:0] D_2,
  output [4:0] rw_2,
  output [23:0] pc_2,
  output [4:0] rs_2,
  output [4:0] rd_2,
  output [4:0] rt_,
  output MemToReg_2,
  output RegW_2,
  output MemRead_2,
  output [31:0] inst,
  output [5:0] funct_2
);

  wire clk_t;

  not not_1 (clk_t, clk);
  Register #(.width(32)) register_1 (.D(RA), .Q(RA_2), .clk(clk_t), .clr(reset));  // open: en
  Register #(.width(6)) register_2 (.D(opcode), .Q(opcode_2), .clk(clk_t), .clr(reset));  // open: en
  Register #(.width(32)) register_3 (.D(D), .Q(D_2), .clk(clk_t), .clr(reset));  // open: en
  Register #(.width(5)) register_4 (.D(rw), .Q(rw_2), .clk(clk_t), .clr(reset));  // open: en
  Register #(.width(24)) register_5 (.D(pc), .Q(pc_2), .clk(clk_t), .clr(reset));  // open: en
  Register #(.width(5)) register_6 (.D(rs), .Q(rs_2), .clk(clk_t), .clr(reset));  // open: en
  Register #(.width(5)) register_7 (.D(rd), .Q(rd_2), .clk(clk_t), .clr(reset));  // open: en
  Register #(.width(5)) register_8 (.D(rt), .Q(rt_), .clk(clk_t), .clr(reset));  // open: en
  Register #(.width(1)) register_9 (.D(MemToReg), .Q(MemToReg_2), .clk(clk_t), .clr(reset));  // open: en
  Register #(.width(1)) register_10 (.D(Regw), .Q(RegW_2), .clk(clk_t), .clr(reset));  // open: en
  Register #(.width(1)) register_11 (.D(MemRead), .Q(MemRead_2), .clk(clk_t), .clr(reset));  // open: en
  Register #(.width(6)) register_12 (.D(funct), .Q(funct_2), .clk(clk_t), .clr(reset));  // open: en

  assign inst = instruccion;

  // Other names for the same wires on the sheet: res = reset
endmodule

module Display (
  input  [31:0] inst,
  input  [5:0] funct,
  output a,
  output b,
  output c,
  output d,
  output e,
  output f,
  output g,
  output h
);

  wire and_2_out, and_3_out, and_4_out, and_5_out, and_6_out, and_7_out, and_8_out, and_9_out, and_10_out,
       and_11_out, and_12_out, and_13_out, and_14_out, and_15_out, and_16_out, and_17_out, and_18_out,
       and_19_out, and_20_out, and_21_out, and_22_out, and_23_out, and_24_out, and_25_out, and_26_out,
       and_27_out, and_28_out, and_29_out, comparator_1_eq, comparator_2_eq, comparator_3_eq, not_1_out,
       not_2_out, not_3_out, not_4_out, not_5_out, not_6_out, not_7_out, not_8_out, not_9_out, not_10_out,
       not_11_out, not_12_out, not_13_out, not_14_out, not_15_out, not_16_out, not_17_out, not_18_out,
       not_19_out, not_20_out, not_21_out, not_22_out, not_23_out, not_24_out, not_25_out, not_26_out,
       not_27_out, sign;
  wire [5:0] multiplexer_1_out, multiplexer_2_out;

  Multiplexer #(.width(6)) multiplexer_1 (
    .in0(inst[31:26]), .in1(6'b101011), .out(multiplexer_1_out), .sel(sign));  // open: en
  Multiplexer #(.width(6)) multiplexer_2 (
    .in0(multiplexer_1_out), .in1(6'b110011), .out(multiplexer_2_out), .sel(comparator_1_eq));  // open: en
  Comparator #(.width(32)) comparator_1 (.a(inst), .b({32{1'b0}}), .eq(comparator_1_eq));  // open: gt, lt
  and and_1 (sign, comparator_2_eq, comparator_3_eq);
  Comparator #(.width(6)) comparator_2 (.a(inst[31:26]), .b({6{1'b0}}), .eq(comparator_2_eq));  // open: gt, lt
  Comparator #(.width(6)) comparator_3 (.a(funct), .b(6'b100010), .eq(comparator_3_eq));  // open: gt, lt
  and and_2 (and_2_out, multiplexer_2_out[0], multiplexer_2_out[1], multiplexer_2_out[4], multiplexer_2_out[5]);
  not not_1 (not_1_out, multiplexer_2_out[1]);
  not not_2 (not_2_out, multiplexer_2_out[0]);
  not not_3 (not_3_out, multiplexer_2_out[3]);
  not not_4 (not_4_out, multiplexer_2_out[0]);
  not not_5 (not_5_out, multiplexer_2_out[0]);
  not not_6 (not_6_out, multiplexer_2_out[3]);
  not not_7 (not_7_out, multiplexer_2_out[1]);
  not not_8 (not_8_out, multiplexer_2_out[3]);
  not not_9 (not_9_out, multiplexer_2_out[3]);
  not not_10 (not_10_out, multiplexer_2_out[4]);
  not not_11 (not_11_out, multiplexer_2_out[3]);
  not not_12 (not_12_out, multiplexer_2_out[5]);
  not not_13 (not_13_out, multiplexer_2_out[3]);
  not not_14 (not_14_out, multiplexer_2_out[3]);
  not not_15 (not_15_out, multiplexer_2_out[1]);
  not not_16 (not_16_out, multiplexer_2_out[2]);
  not not_17 (not_17_out, multiplexer_2_out[0]);
  not not_18 (not_18_out, multiplexer_2_out[2]);
  not not_19 (not_19_out, multiplexer_2_out[4]);
  not not_20 (not_20_out, multiplexer_2_out[3]);
  not not_21 (not_21_out, multiplexer_2_out[5]);
  not not_22 (not_22_out, multiplexer_2_out[0]);
  not not_23 (not_23_out, multiplexer_2_out[2]);
  not not_24 (not_24_out, multiplexer_2_out[3]);
  not not_25 (not_25_out, multiplexer_2_out[4]);
  not not_26 (not_26_out, multiplexer_2_out[5]);
  not not_27 (not_27_out, multiplexer_2_out[1]);
  or or_1 (a, multiplexer_2_out[3], multiplexer_2_out[2], and_2_out);
  and and_3 (and_3_out, not_1_out, multiplexer_2_out[3]);
  and and_4 (and_4_out, not_2_out, multiplexer_2_out[1]);
  and and_5 (and_5_out, multiplexer_2_out[1], not_3_out, multiplexer_2_out[4], multiplexer_2_out[5]);
  and and_6 (and_6_out, not_4_out, multiplexer_2_out[1]);
  and and_7 (and_7_out, multiplexer_2_out[1], multiplexer_2_out[4], multiplexer_2_out[5]);
  and and_8 (and_8_out, not_5_out, not_6_out);
  and and_9 (and_9_out, not_7_out, not_8_out);
  and and_10 (and_10_out, not_9_out, not_10_out);
  and and_11 (and_11_out, not_11_out, not_12_out);
  and and_12 (and_12_out, multiplexer_2_out[2], not_13_out);
  and and_13 (and_13_out, multiplexer_2_out[1], multiplexer_2_out[3]);
  and and_14 (and_14_out, not_14_out, multiplexer_2_out[5]);
  and and_15 (and_15_out, not_15_out, multiplexer_2_out[3]);
  and and_16 (and_16_out, not_16_out, multiplexer_2_out[5]);
  and and_17 (and_17_out, not_17_out, multiplexer_2_out[3]);
  and and_18 (and_18_out, not_18_out, multiplexer_2_out[3]);
  and and_19 (and_19_out, multiplexer_2_out[3], not_19_out);
  and and_20 (and_20_out, multiplexer_2_out[2], not_20_out);
  and and_21 (and_21_out, multiplexer_2_out[2], not_21_out);
  and and_22 (and_22_out, multiplexer_2_out[1], multiplexer_2_out[2]);
  and and_23 (and_23_out, not_22_out, multiplexer_2_out[3]);
  and and_24 (and_24_out, not_23_out, multiplexer_2_out[3]);
  and and_25 (and_25_out, multiplexer_2_out[2], not_24_out);
  and and_26 (and_26_out, multiplexer_2_out[2], not_25_out);
  and and_27 (and_27_out, multiplexer_2_out[2], not_26_out);
  and and_28 (and_28_out, multiplexer_2_out[1], multiplexer_2_out[3]);
  and and_29 (and_29_out, not_27_out, multiplexer_2_out[3]);
  or or_2 (b, and_3_out, multiplexer_2_out[2], and_4_out, and_5_out);
  or or_3 (c, multiplexer_2_out[3], multiplexer_2_out[2], and_6_out, and_7_out);
  or or_4 (d, and_8_out, and_9_out, and_10_out, and_11_out, and_12_out, and_13_out);
  or or_5 (e, and_14_out, and_15_out, multiplexer_2_out[2]);
  or or_6 (f, and_16_out, and_17_out, and_18_out, and_19_out, and_20_out, and_21_out, and_22_out);
  or or_7 (g, and_23_out, and_24_out, and_25_out, and_26_out, and_27_out, and_28_out);
  or or_8 (h, and_29_out, sign);

  // Other names for the same wires on the sheet: opcod[5:0] = inst[31:26]
endmodule

module displaypc (
  input  [23:0] pc,
  output [3:0] display1,
  output [3:0] display2,
  output [3:0] display3,
  output [3:0] display4
);

  wire [7:4] bit_extender_1_out, bit_extender_2_out;
  wire [23:0] divider_1_out, divider_1_rem;

  Divider #(.width(24)) divider_1 (.a(pc), .b(24'ha), .out(divider_1_out), .rem(divider_1_rem));  // open: upper
  Bit_Extender #(.in_width(24), .out_width(8)) bit_extender_1 (
    .in(divider_1_rem), .out({bit_extender_1_out, display2}));
  Bit_Extender #(.in_width(24), .out_width(8)) bit_extender_2 (
    .in(divider_1_out), .out({bit_extender_2_out, display1}));
  Bit_Extender #(.in_width(24), .out_width(8)) bit_extender_3 (.in(pc), .out({display4, display3}));
endmodule

// Hazard
module hazard (
  input  [23:0] Ins1,
  input  [23:0] Ins2,
  input  [4:0] Rt,
  input  [4:0] Rd,
  input  clock,
  input  [4:0] Rt_Rd,
  input  [4:0] Rs,
  input  [4:0] Rt_Rd_2,
  input  [31:0] InsF,
  output Stall
);

  wire and_1_out, and_2_out, comparator_1_eq, comparator_2_eq, comparator_3_eq, comparator_4_eq,
       comparator_5_eq, comparator_6_eq, comparator_7_eq, comparator_8_eq, not_1_out, or_1_out, or_2_out;

  Comparator #(.width(5)) comparator_1 (.a(Rt), .b(Rt_Rd_2), .eq(comparator_1_eq));  // open: gt, lt
  Comparator #(.width(5)) comparator_2 (.a(Rd), .b(Rt_Rd_2), .eq(comparator_2_eq));  // open: gt, lt
  Comparator #(.width(5)) comparator_3 (.a(Rs), .b(Rt_Rd_2), .eq(comparator_3_eq));  // open: gt, lt
  Comparator #(.width(5)) comparator_4 (.a(Rt), .b(Rt_Rd), .eq(comparator_4_eq));  // open: gt, lt
  Comparator #(.width(5)) comparator_5 (.a(Rd), .b(Rt_Rd), .eq(comparator_5_eq));  // open: gt, lt
  Comparator #(.width(5)) comparator_6 (.a(Rt_Rd), .b(Rs), .eq(comparator_6_eq));  // open: gt, lt
  not not_1 (not_1_out, comparator_7_eq);
  Comparator #(.width(24)) comparator_7 (.a(Ins2), .b(Ins1), .eq(comparator_7_eq));  // open: gt, lt
  or or_1 (or_1_out, comparator_4_eq, comparator_6_eq, comparator_5_eq);
  and and_1 (and_1_out, or_1_out, not_1_out);
  or or_2 (or_2_out, comparator_1_eq, comparator_3_eq, comparator_2_eq);
  Comparator #(.width(32)) comparator_8 (.a({32{1'b0}}), .b(InsF), .eq(comparator_8_eq));  // open: gt, lt
  and and_2 (and_2_out, or_2_out, comparator_8_eq);
  S_R_Flip_Flop #(.trigger("high")) s_r_ff_1 (
    .S(and_1_out), .R(and_2_out), .Q(Stall));  // open: clk, Qn, preset, reset, en
endmodule

// Forward
module forward (
  input  EX_MEM_RegWrite,
  input  [4:0] EX_MEM_Rd,
  input  [4:0] ID_EX_Rt,
  input  [4:0] ID_EX_Rs,
  input  MEM_WB_RegWr,
  input  [4:0] MEM_WB_Rd,
  output hazard,
  output [1:0] ForwardA,
  output [1:0] ForwardB
);

  wire comparator_1_eq, comparator_2_eq, comparator_3_eq, comparator_4_eq, comparator_5_eq, comparator_6_eq,
       comparator_7_eq, comparator_8_eq;

  Comparator #(.width(5)) comparator_1 (.a(EX_MEM_Rd), .b({5{1'b0}}), .eq(comparator_1_eq));  // open: gt, lt
  Comparator #(.width(5)) comparator_2 (.a(EX_MEM_Rd), .b(ID_EX_Rs), .eq(comparator_2_eq));  // open: gt, lt
  Comparator #(.width(5)) comparator_3 (.a(EX_MEM_Rd), .b(ID_EX_Rt), .eq(comparator_3_eq));  // open: gt, lt
  Comparator #(.width(5)) comparator_4 (.a({5{1'b0}}), .b(MEM_WB_Rd), .eq(comparator_4_eq));  // open: gt, lt
  Comparator #(.width(5)) comparator_5 (.a(EX_MEM_Rd), .b(ID_EX_Rs), .eq(comparator_5_eq));  // open: gt, lt
  Comparator #(.width(5)) comparator_6 (.a(MEM_WB_Rd), .b(ID_EX_Rs), .eq(comparator_6_eq));  // open: gt, lt
  Comparator #(.width(5)) comparator_7 (.a(EX_MEM_Rd), .b(ID_EX_Rt), .eq(comparator_7_eq));  // open: gt, lt
  Comparator #(.width(5)) comparator_8 (.a(MEM_WB_Rd), .b(ID_EX_Rt), .eq(comparator_8_eq));  // open: gt, lt
  and and_1 (ForwardA[1], ~comparator_1_eq, EX_MEM_RegWrite, comparator_2_eq);  // AND_Gate
  and and_2 (ForwardB[1], ~comparator_1_eq, comparator_3_eq, EX_MEM_RegWrite);  // AND_Gate
  and and_3 (ForwardA[0], MEM_WB_RegWr, ~comparator_4_eq, ~comparator_5_eq, comparator_6_eq);  // AND_Gate
  and and_4 (ForwardB[0], MEM_WB_RegWr, ~comparator_4_eq, ~comparator_7_eq, comparator_8_eq);  // AND_Gate
  or or_1 (hazard, ForwardA[1], ForwardB[1], ForwardA[0], ForwardB[0]);

  // Notes on the sheet:
  //   1if-> fa=2  10
  //   2if ->fb= 2 10
  //   3if ->fa =1 01
  //   4 if ->fb= 1 01
endmodule
